// Logisim project Parie1.circ as structural Verilog: 3 circuits, main circuit unité de calcul
module \unité_de_calcul  (
  input  [7:0] in_1,
  input  [7:0] in_2,
  input  in_3,
  input  in_4,
  input  in_5,
  output [7:0] out_6,
  output out_7
);

  wire adder_1_cout, subtractor_1_bout;
  wire [7:0] adder_1_out, subtractor_1_out, \séquenseur_1_p6 , \séquenseur_1_p7 , \séquenseur_1_p11 ,
       \séquenseur_1_p12 ;

  Adder adder_1 (.a(in_1), .b(in_2), .out(adder_1_out), .cout(adder_1_cout));  // open: cin
  Subtractor subtractor_1 (.a(in_1), .b(in_2), .out(subtractor_1_out), .bout(subtractor_1_bout));  // open: bin
  // Séquenseur séquenseur_1: pin names not known; wires that end beside it: in_3, in_4, in_5, adder_1_out, subtractor_1_out, \séquenseur_1_p6 , \séquenseur_1_p7 , out_7, adder_1_cout, subtractor_1_bout, \séquenseur_1_p11 , \séquenseur_1_p12 , out_6
  Multiplier multiplier_1 (.a(in_1), .b(in_2), .out(\séquenseur_1_p6 ), .cout(\séquenseur_1_p11 ));  // open: cin
  Divider divider_1 (.a(in_1), .b(in_2), .out(\séquenseur_1_p7 ), .rem(\séquenseur_1_p12 ));  // open: upper
endmodule

module \Séquenseur  (
  input  in_1,
  input  in_2,
  input  in_3,
  input  in_4,
  input  [7:0] in_5,
  input  [7:0] in_6,
  input  [7:0] in_7,
  input  [7:0] in_8,
  input  in_9,
  input  in_10,
  input  in_11,
  output [7:0] out_12,
  output out_13
);

  wire and_1_out, and_2_out, and_3_out, and_4_out, and_5_out, and_6_out, and_7_out, and_8_out, nor_1_out,
       nor_2_p3, nor_2_p4, nor_3_out, not_1_out, or_1_out, or_2_p3, or_2_p5, undriven, undriven_2;
  wire [7:0] \valideur_d_octét_1_out_3 , \valideur_d_octét_2_out_3 , \valideur_d_octét_3_out_3 ,
       \valideur_d_octét_4_out_3 ;

  and and_1 (and_1_out, in_9, in_10, undriven);
  nor nor_1 (nor_1_out, in_10, undriven, in_10, in_10, nor_2_p4);
  // NOR_Gate nor_2: pin names not known; wires that end beside it: in_10, in_11, nor_2_p3, nor_2_p4, in_9
  nor nor_3 (nor_3_out, nor_2_p3, in_9, in_11);
  not not_1 (not_1_out, in_11);
  and and_2 (and_2_out, in_1, and_3_out);
  and and_3 (and_3_out, in_9, nor_2_p4);
  and and_4 (and_4_out, in_10, nor_3_out, undriven_2);
  and and_5 (and_5_out, undriven_2, and_1_out, not_1_out);
  and and_6 (and_6_out, nor_1_out, in_11);
  and and_7 (and_7_out, in_2, and_4_out);
  and and_8 (and_8_out, in_3, and_5_out);
  or or_1 (or_1_out, and_2_out, and_7_out);
  // OR_Gate or_2: pin names not known; wires that end beside it: or_1_out, and_8_out, or_2_p3, and_8_out, or_2_p5
  or or_3 (out_13, or_1_out, or_2_p3);
  \Valideur_d_octét  \valideur_d_octét_1  (.in_2(and_3_out), .in_1(in_5), .out_3(\valideur_d_octét_1_out_3 ));
  \Valideur_d_octét  \valideur_d_octét_2  (.in_2(and_4_out), .in_1(in_6), .out_3(\valideur_d_octét_2_out_3 ));
  \Valideur_d_octét  \valideur_d_octét_3  (.in_2(and_5_out), .in_1(in_7), .out_3(\valideur_d_octét_3_out_3 ));
  \Valideur_d_octét  \valideur_d_octét_4  (.in_2(and_6_out), .in_1(in_8), .out_3(\valideur_d_octét_4_out_3 ));
  and and_9 (or_2_p5, in_4, and_6_out);
  assign out_12 = \valideur_d_octét_1_out_3  | \valideur_d_octét_2_out_3  | \valideur_d_octét_3_out_3  | \valideur_d_octét_4_out_3 ;  // OR_Gate or_4, 8 bits wide
endmodule

module \Valideur_d_octét  (
  input  [7:0] in_1,
  input  in_2,
  output [7:0] out_3
);

  wire undriven, undriven_2, undriven_3, undriven_4, undriven_5, undriven_6, undriven_7;

  and and_1 (out_3[7], in_2, in_1[7], undriven);
  and and_2 (out_3[6], undriven, in_2, in_1[6], undriven_2);
  and and_3 (out_3[5], undriven_2, in_2, in_1[5], undriven_3);
  and and_4 (out_3[3], undriven_4, in_2, in_1[3], undriven_5);
  and and_5 (out_3[4], undriven_3, in_2, in_1[4], undriven_4);
  and and_6 (out_3[1], undriven_6, in_2, in_1[1], undriven_7);
  and and_7 (out_3[2], undriven_5, in_2, in_1[2], undriven_6);
  and and_8 (out_3[0], undriven_7, in_2, in_1[0]);
endmodule
